# Fritzing sketch Sketch (saved by Fritzing 0.9.10b)

parts:
  Componente1 = Arduino Nano (Rev3.0)
  Componente2 = Adafruit Motor/Stepper/Servo Shield [part_number="Adafruit #1438"]
  A1 = DFRobot I2C Digital Wattmeter

nets:
  GND: Componente1.GND, Componente2.GND, A1.Pin_5, A1.Pin_10
  5V: Componente1.5V, Componente2.+5V, A1.Pin_4, A1.Pin_11
  N1: Componente1.A5, A1.Pin_6, A1.Pin_9
  N2: Componente1.A4, A1.Pin_7, A1.Pin_8
  N3: Componente2.VMOTOR, A1.Pin_3

notes:
  12V GND
  MOT CH A - MOT CH B - GND - ENC VCC - ENC CH A - ENC CH B

custom parts:
  Adafruit Motor/Stepper/Servo Shield: The original Adafruit Motorshield kit is one of our most beloved kits, which is why we decided to make something even better. We have upgraded the shield kit to make the bestest, easiest way to drive DC and Stepper motors. This shield will make quick work of your next robotics project! We kept the ability to drive up to 4 DC motors or 2 stepper motors, but added many improvements: Instead of a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
  DFRobot I2C Digital Wattmeter: Gravity: I2C Digital Wattmeter is a high-resolution, high-precision, large-scale measurement module that can measure the voltage, current and power of various electronic modules and electrical equipment within 26V 8A, and the maximum relative error is no more than ±0.2%.
